# Fritzing sketch BBB_7segment_dojo (saved by Fritzing 0.8.3b)
breadboards: 1

parts:
  BeagleBone1 = BeagleBone Black
  U1 = POT [package=pot_mammoth]
  7_Segment1 = 7 Segment Display
  R1 = Resistor [tolerance=±5% resistance=150 package=THT]
  R2 = Resistor [tolerance=±5% resistance=150 package=THT]
  R3 = Resistor [tolerance=±5% resistance=150 package=THT]
  R4 = Resistor [tolerance=±5% resistance=150 package=THT]
  R5 = Resistor [tolerance=±5% resistance=150 package=THT]
  R6 = Resistor [tolerance=±5% resistance=150 package=THT]
  R7 = Resistor [tolerance=±5% resistance=150 package=THT]
  R8 = Resistor [tolerance=±5% resistance=150 package=THT]

nets:
  N1: BeagleBone1.no_name_yet#32, U1.E
  N2: BeagleBone1.no_name_yet#33, U1.A
  N3: BeagleBone1.no_name_yet#102, U1.S, 7_Segment1.common_anode
  N4: BeagleBone1.no_name_yet#112, R1.Pin_1
  N5: BeagleBone1.no_name_yet#113, R2.Pin_1
  N6: BeagleBone1.no_name_yet#114, R5.Pin_1
  N7: BeagleBone1.no_name_yet#115, R7.Pin_0
  N8: BeagleBone1.no_name_yet#116, R8.Pin_0
  N9: BeagleBone1.no_name_yet#117, R3.Pin_0
  N10: BeagleBone1.no_name_yet#118, R4.Pin_0
  N11: BeagleBone1.no_name_yet#119, R6.Pin_1
  N12: 7_Segment1.Segment_E, R8.Pin_1
  N13: 7_Segment1.Segment_D, R7.Pin_1
  N14: 7_Segment1.Segment_C, R5.Pin_0
  N15: 7_Segment1.Segment_DP, R6.Pin_0
  N16: 7_Segment1.Segment_B, R2.Pin_0
  N17: 7_Segment1.Segment_A, R1.Pin_0
  N18: 7_Segment1.Segment_F, R3.Pin_1
  N19: 7_Segment1.Segment_G, R4.Pin_1

custom parts:
  BeagleBone Black: BeagleBone Black rev. A5B
